# Fritzing sketch Prototype (saved by Fritzing 0.9.3b)
breadboards: 1

parts:
  Part1 = Arduino Uno (Rev3)
  J1 = Basic Servo
  Motor_1 = DC Motor
  Motor_2 = DC Motor
  Ultra_sonic_sensor = hc-sr04
  Color_Sensor = HDJD-S822-QR999 [package=qfn-16]
  Motor_Driver = Dual VNH2SP30 Motor Driver [part_number=MD03A]
  LiPo_Battery = Battery Holders [package=lipo-1100mAh]
  Power_Distribution_board = Arduino Power Driver Shield

nets:
  N1: Part1.A4/SDA, Color_Sensor.GSBLUE1
  N2: Part1.A5/SCL, Color_Sensor.GSRED0
  N3: Part1.D9_PWM, J1.pulse
  N4: Part1.D11_PWM/MOSI, Motor_Driver.1DIAG/EN
  N5: Part1.D12/MISO, Ultra_sonic_sensor.Echo
  N6: Part1.D13/SCK, Ultra_sonic_sensor.Trig
  GND: Part1.GND, J1.gnd, Ultra_sonic_sensor.GND, Color_Sensor.GND
  N7: Part1.D3_PWM, Motor_Driver.2DIAG/EN
  N8: Part1.D4, Motor_Driver.2INb#143
  N9: Part1.D5_PWM, Motor_Driver.2INb#142
  N10: Part1.D7, Motor_Driver.1INa
  VCC: Part1.5V, J1.vcc, Ultra_sonic_sensor.VCC, Color_Sensor.VDD3
  N11: Motor_1.pin_1, Motor_Driver.OUT_2A
  N12: Motor_1.pin_2, Motor_Driver.OUT_2B
  N13: Motor_2.pin_1, Motor_Driver.OUT_1A
  N14: Motor_2.pin_2, Motor_Driver.OUT_1B
  VIN: Motor_Driver.VIN, Power_Distribution_board.12V
  N15: Motor_Driver.GND, Power_Distribution_board.D6-12V
  N16: LiPo_Battery.+, Power_Distribution_board.VIN
  N17: LiPo_Battery.-, Power_Distribution_board.GND
